# Fritzing sketch StartRestart (saved by Fritzing 0.9.3b)
breadboards: 1

parts:
  Part1 = Arduino Uno (Rev3)
  LED1 = RGB LED (com. cathode, rgb) [package="5 mm [THT]"]
  VCC1 = Battery
  LED2 = RGB LED (com. cathode, rgb) [package="5 mm [THT]"]

nets:
  N1: Part1.D8, LED2.common_cathode
  N2: Part1.D9_PWM, LED1.common_cathode
  N3: Part1.5V, LED1.green_anode, LED2.green_anode
  N4: LED1.red_anode, VCC1.+, LED2.red_anode
  N5: LED1.blue_anode, VCC1.-, LED2.blue_anode
